# Fritzing sketch Diagram (saved by Fritzing 0.9.3b)
circuit board: 27.3863cm x 15.0376cm

parts:
  CPU1 = NodeMCU WROOM ESP 32
  A1 = DHT22 module
  VCC1 = Battery
  LED1 = smd LED [color="Red (633nm)" package="0805 [SMD]"]
  A2 = 3 channel relay module
  Part1 = Soil Moisture Sensor
  U1 = LCD-16X2 [package=lcd-16x2_noholes]
  R1 = Rotary Potentiometer (Large) [maximum_resistance=100kΩ package=THT]
  Water_Level_Sensor1 = Water Level Sensor

nets:
  N1: CPU1.pin_5, Water_Level_Sensor1.SIG
  N2: CPU1.pin_6, Part1.SIG
  N3: CPU1.pin_8, CPU1.pin_24, A2.Pin_2, U1.DB7
  N4: CPU1.pin_9, U1.DB6
  N5: CPU1.pin_10, U1.DB5
  N6: CPU1.pin_11, U1.DB4
  N7: CPU1.pin_12, U1.E
  N8: CPU1.pin_13, U1.RS
  GND: CPU1.pin_15, A1.GND, VCC1.-, LED1.cathode, A2.Pin_1, Part1.GND, U1.VSS, U1.R_W, U1.K, R1.leg1
  VCC: CPU1.pin_16, A1.VCC, VCC1.+, A2.Pin_5, Part1.VCC, U1.VDD, U1.A, Water_Level_Sensor1.VCC
  N9: CPU1.pin_20, LED1.anode
  N10: CPU1.pin_21, A1.DAT
  N11: U1.VO, R1.wiper

custom parts:
  NodeMCU WROOM ESP 32: 30 pol Development Kit
  DHT22 module: DHT22 module. Pins GND VCC Data.
  3 channel relay module: This product is 3 channel self-locking and interlocking relay function.Keep button on 3 second when set tirgger level. it will automatic switchover self-locking and interlock function. 3 channel self-locking function:Press the corresponding button,the corresppond relay on,press again,relay off. 3 channel interlock function:Press the corresponding button,the corresppond relay on,but other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
  Water Level Sensor: A water level sensor. This sensor operates at 3V to 5V. The Sig (signal) pin outputs an analogue signal that is in proportion to the amount of water in contact with the sensor.
